# Fritzing sketch transmitter (saved by Fritzing 0.9.4)
breadboards: 2

parts:
  R1 = Resistor [tolerance=±5% resistance=10k package="0805 [SMD]"]
  MOTOR4 = 28BYJ-48 Stepper Motor
  Part1 = Arduino Uno (Rev3)
  S2 = Pushbutton [package="[THT]"]
  HC-SR04_Sensor_3 = HC-SR04 Ultrasonic Distance Sensor
  X2 = X113647 Stepper Driver Board [part_number=X113647 package=board]
  Part2 = Bluetooth module [part_number=101240]
  LED1 = LED - 3mm [color="Red (633nm)" package="3 mm [THT]"]
  R2 = Resistor [tolerance=±5% resistance=220 package="0402 [SMD]"]

nets (from the breadboard view):
  N1: R1.Pin_0, Part1.D7, S2.Pin_1, S2.Pin_2
  GND: R1.Pin_1, Part1.GND, HC-SR04_Sensor_3.GND, X2.GND, Part2.GND, R2.Pin_0
  N2: MOTOR4.BLUE, X2.BLUE
  N3: MOTOR4.PINK, X2.PINK
  N4: MOTOR4.RED, X2.RED
  N5: MOTOR4.ORANGE, X2.ORANGE
  N6: MOTOR4.YELLOW, X2.YELLOW
  N7: Part1.D8, X2.IN1
  N8: Part1.D9_PWM, X2.IN3
  N9: Part1.D10_PWM/SS, X2.IN2
  N10: Part1.D11_PWM/MOSI, X2.IN4
  N11: Part1.D2, HC-SR04_Sensor_3.TRIG
  N12: Part1.D3_PWM, HC-SR04_Sensor_3.ECHO
  N13: Part1.D4, Part2.TX
  N14: Part1.D5_PWM, Part2.RX
  N15: Part1.D6_PWM, LED1.anode
  VCC: Part1.5V, S2.Pin_3, S2.Pin_4, HC-SR04_Sensor_3.VCC, X2.+V, Part2.VCC
  N16: LED1.cathode, R2.Pin_1

custom parts:
  28BYJ-48 Stepper Motor: 28BYJ-48 gear-reduction stepper motor (small)
  HC-SR04 Ultrasonic Distance Sensor: The HC-SR04 is an ultrasonic distance sensor. It is capable of providing measurement for ranges of 2cm to 400cm. The module operates at 5V.
  X113647 Stepper Driver Board: A common stepper motor driver board based on ULN2003APG darlington array
